// Logisim project P0_CRC.circ as structural Verilog: 2 circuits, main circuit CRC
module CRC (
  input  [7:0] to_div,
  input  [3:0] div,
  output [10:0] out_3
);

  wire [2:0] n4_bit_div_1_out_3, n4_bit_div_2_out_3, n4_bit_div_3_out_3, n4_bit_div_4_out_3,
       n4_bit_div_6_out_3, n4_bit_div_7_out_3, temp;

  _4_bit_div u_4_bit_div_1 (.in_1({temp, 1'b0}), .div(div), .out_3(n4_bit_div_1_out_3));
  _4_bit_div u_4_bit_div_2 (.in_1(to_div[7:4]), .div(div), .out_3(n4_bit_div_2_out_3));
  _4_bit_div u_4_bit_div_3 (.in_1({n4_bit_div_1_out_3, 1'b0}), .div(div), .out_3(n4_bit_div_3_out_3));
  _4_bit_div u_4_bit_div_4 (.in_1({n4_bit_div_2_out_3, to_div[3]}), .div(div), .out_3(n4_bit_div_4_out_3));
  _4_bit_div u_4_bit_div_5 (.in_1({n4_bit_div_3_out_3, 1'b0}), .div(div), .out_3(out_3[2:0]));
  _4_bit_div u_4_bit_div_6 (.in_1({n4_bit_div_4_out_3, to_div[2]}), .div(div), .out_3(n4_bit_div_6_out_3));
  _4_bit_div u_4_bit_div_7 (.in_1({n4_bit_div_6_out_3, to_div[1]}), .div(div), .out_3(n4_bit_div_7_out_3));
  _4_bit_div u_4_bit_div_8 (.in_1({n4_bit_div_7_out_3, to_div[0]}), .div(div), .out_3(temp));

  assign out_3[10:3] = to_div;
endmodule

module _4_bit_div (
  input  [3:0] in_1,
  input  [3:0] div,
  output [2:0] out_3
);

  wire [3:0] ex_high, real_div;
  wire [3:3] xor_1_out;

  assign real_div = ex_high & div;  // AND_Gate and_1, 4 bits wide
  assign {xor_1_out[3], out_3} = real_div ^ in_1;  // XOR_Gate xor_1, 4 bits wide
  assign ex_high = {{3{in_1[3]}}, in_1[3]};  // Bit_Extender bit_extender_1
  // Probe on ex_high

  // Other names for the same wires on the sheet: to_div[3:0] = in_1
endmodule
