// Logisim project P0_GRF.circ as structural Verilog: 1 circuit, main circuit grf
module grf (
  input  in_1,
  input  in_2,
  input  in_3,
  input  [4:0] A1,
  input  [4:0] A2,
  input  [4:0] A3,
  input  [31:0] WD,
  output [31:0] RD1,
  output [31:0] RD2
);

  wire _0, _1, _2, _3, _4, _5, _6, _7, _8, _9, _10, _11, _12, _13, _14, _15, _16, _17, _18, _19, _20, _21,
       _22, _23, _24, _25, _26, _27, _28, _29, _30, _31;
  wire [31:0] out_0, out_1, out_2, out_3, out_4, out_5, out_6, out_7, out_8, out_9, out_10, out_11, out_12,
       out_13, out_14, out_15, out_16, out_17, out_18, out_19, out_20, out_21, out_22, out_23, out_24,
       out_25, out_26, out_27, out_28, out_29, out_30, out_31;

  Demultiplexer #(.select(5), .disabled(0), .enable("false")) demultiplexer_1 (
    .out0(_0), .out1(_1), .out2(_2), .out3(_3), .out4(_4), .out5(_5), .out6(_6), .out7(_7), .out8(_8),
    .out9(_9), .out10(_10), .out11(_11), .out12(_12), .out13(_13), .out14(_14), .out15(_15), .out16(_16),
    .out17(_17), .out18(_18), .out19(_19), .out20(_20), .out21(_21), .out22(_22), .out23(_23), .out24(_24),
    .out25(_25), .out26(_26), .out27(_27), .out28(_28), .out29(_29), .out30(_30), .out31(_31), .in(in_3),
    .sel(A3));
  Register #(.width(32)) u__0 (.D(WD), .en(_0), .Q(out_0), .clk(in_1), .clr(1'b1));
  Register #(.width(32)) u__1 (.D(WD), .en(_1), .Q(out_1), .clk(in_1), .clr(in_2));
  Register #(.width(32)) u__2 (.D(WD), .en(_2), .Q(out_2), .clk(in_1), .clr(in_2));
  Register #(.width(32)) u__3 (.D(WD), .en(_3), .Q(out_3), .clk(in_1), .clr(in_2));
  Register #(.width(32)) u__4 (.D(WD), .en(_4), .Q(out_4), .clk(in_1), .clr(in_2));
  Register #(.width(32)) u__5 (.D(WD), .en(_5), .Q(out_5), .clk(in_1), .clr(in_2));
  Register #(.width(32)) u__6 (.D(WD), .en(_6), .Q(out_6), .clk(in_1), .clr(in_2));
  Register #(.width(32)) u__7 (.D(WD), .en(_7), .Q(out_7), .clk(in_1), .clr(in_2));
  Register #(.width(32)) u__9 (.D(WD), .en(_9), .Q(out_9), .clk(in_1), .clr(in_2));
  Register #(.width(32)) u__10 (.D(WD), .en(_10), .Q(out_10), .clk(in_1), .clr(in_2));
  Register #(.width(32)) u__11 (.D(WD), .en(_11), .Q(out_11), .clk(in_1), .clr(in_2));
  Register #(.width(32)) u__12 (.D(WD), .en(_12), .Q(out_12), .clk(in_1), .clr(in_2));
  Register #(.width(32)) u__13 (.D(WD), .en(_13), .Q(out_13), .clk(in_1), .clr(in_2));
  Register #(.width(32)) u__14 (.D(WD), .en(_14), .Q(out_14), .clk(in_1), .clr(in_2));
  Register #(.width(32)) u__15 (.D(WD), .en(_15), .Q(out_15), .clk(in_1), .clr(in_2));
  Register #(.width(32)) u__8 (.D(WD), .en(_8), .Q(out_8), .clk(in_1), .clr(in_2));
  Register #(.width(32)) u__16 (.D(WD), .en(_16), .Q(out_16), .clk(in_1), .clr(in_2));
  Register #(.width(32)) u__17 (.D(WD), .en(_17), .Q(out_17), .clk(in_1), .clr(in_2));
  Register #(.width(32)) u__18 (.D(WD), .en(_18), .Q(out_18), .clk(in_1), .clr(in_2));
  Register #(.width(32)) u__19 (.D(WD), .en(_19), .Q(out_19), .clk(in_1), .clr(in_2));
  Register #(.width(32)) u__20 (.D(WD), .en(_20), .Q(out_20), .clk(in_1), .clr(in_2));
  Register #(.width(32)) u__21 (.D(WD), .en(_21), .Q(out_21), .clk(in_1), .clr(in_2));
  Register #(.width(32)) u__22 (.D(WD), .en(_22), .Q(out_22), .clk(in_1), .clr(in_2));
  Register #(.width(32)) u__23 (.D(WD), .en(_23), .Q(out_23), .clk(in_1), .clr(in_2));
  Register #(.width(32)) u__24 (.D(WD), .en(_24), .Q(out_24), .clk(in_1), .clr(in_2));
  Register #(.width(32)) u__25 (.D(WD), .en(_25), .Q(out_25), .clk(in_1), .clr(in_2));
  Register #(.width(32)) u__26 (.D(WD), .en(_26), .Q(out_26), .clk(in_1), .clr(in_2));
  Register #(.width(32)) u__27 (.D(WD), .en(_27), .Q(out_27), .clk(in_1), .clr(in_2));
  Register #(.width(32)) u__28 (.D(WD), .en(_28), .Q(out_28), .clk(in_1), .clr(in_2));
  Register #(.width(32)) u__29 (.D(WD), .en(_29), .Q(out_29), .clk(in_1), .clr(in_2));
  Register #(.width(32)) u__30 (.D(WD), .en(_30), .Q(out_30), .clk(in_1), .clr(in_2));
  Register #(.width(32)) u__31 (.D(WD), .en(_31), .Q(out_31), .clk(in_1), .clr(in_2));
  Multiplexer #(.select(5), .width(32), .disabled(0), .enable("false")) multiplexer_1 (
    .in0(out_0), .in1(out_1), .in2(out_2), .in3(out_3), .in4(out_4), .in5(out_5), .in6(out_6), .in7(out_7),
    .in8(out_8), .in9(out_9), .in10(out_10), .in11(out_11), .in12(out_12), .in13(out_13), .in14(out_14),
    .in15(out_15), .in16(out_16), .in17(out_17), .in18(out_18), .in19(out_19), .in20(out_20), .in21(out_21),
    .in22(out_22), .in23(out_23), .in24(out_24), .in25(out_25), .in26(out_26), .in27(out_27), .in28(out_28),
    .in29(out_29), .in30(out_30), .in31(out_31), .out(RD1), .sel(A1));
  Multiplexer #(.select(5), .width(32), .disabled(0), .enable("false")) multiplexer_2 (
    .in0(out_0), .in1(out_1), .in2(out_2), .in3(out_3), .in4(out_4), .in5(out_5), .in6(out_6), .in7(out_7),
    .in8(out_8), .in9(out_9), .in10(out_10), .in11(out_11), .in12(out_12), .in13(out_13), .in14(out_14),
    .in15(out_15), .in16(out_16), .in17(out_17), .in18(out_18), .in19(out_19), .in20(out_20), .in21(out_21),
    .in22(out_22), .in23(out_23), .in24(out_24), .in25(out_25), .in26(out_26), .in27(out_27), .in28(out_28),
    .in29(out_29), .in30(out_30), .in31(out_31), .out(RD2), .sel(A2));

  // Other names for the same wires on the sheet: clk = in_1; input[31:0] = WD; reset = in_2; WE = in_3
endmodule
