// Logisim project P0_fsm.circ as structural Verilog: 2 circuits, main circuit fsm
module fsm (
  input  CLR,
  input  [1:0] in_2,
  output out_3
);

  wire clk, not_1_out, reset, s0, s1, status_change_1_s0_prime, status_change_1_s1_prime;

  Clock clock_1 (.out(clk));
  Register #(.width(1)) register_1 (.D(CLR), .Q(reset), .clk(clk), .clr(reset));  // open: en
  not not_1 (not_1_out, in_2[0]);
  and and_1 (out_3, s1, not_1_out);
  status_change status_change_1 (
    .in_0(in_2[0]), .in_1(in_2[1]), .s0(s0), .s1(s1), .s0_prime(status_change_1_s0_prime),
    .s1_prime(status_change_1_s1_prime));
  Register #(.width(1)) u_s0 (.D(status_change_1_s0_prime), .Q(s0), .clk(clk), .clr(reset));  // open: en
  Register #(.width(1)) u_s1 (.D(status_change_1_s1_prime), .Q(s1), .clk(clk), .clr(reset));  // open: en

  // Other names for the same wires on the sheet: in_0 = in_2[0]; input[1:0] = in_2; in_1 = in_2[1]
endmodule

module status_change (
  input  in_0,
  input  in_1,
  input  s0,
  input  s1,
  output s0_prime,
  output s1_prime
);

  wire and_1_out, not_1_out, not_2_out, not_3_out, not_4_out, or_1_out;

  not not_1 (not_1_out, in_1);
  not not_2 (not_2_out, s0);
  not not_3 (not_3_out, s1);
  not not_4 (not_4_out, in_0);
  and and_1 (and_1_out, not_2_out, s1);
  and and_2 (s1_prime, s0, not_4_out);
  or or_1 (or_1_out, and_1_out, not_3_out);
  and and_3 (s0_prime, in_0, not_1_out, or_1_out);
endmodule
