// Logisim project P0_ftoi.circ as structural Verilog: 2 circuits, main circuit ftoi
module ftoi (
  input  [15:0] float,
  output [31:0] \int 
);

  wire and_1_out, nor_1_out, or_1_out;
  wire [31:0] caculater_1_out_4;

  nor nor_1 (nor_1_out, float[10], float[11], float[12], float[13], float[14]);
  and and_1 (and_1_out, float[10], float[11], float[12], float[13], float[14]);
  or or_1 (or_1_out, nor_1_out, and_1_out);
  caculater caculater_1 (.sign(float[15]), .fraction(float[9:0]), .exponent(float[14:10]), .out_4(caculater_1_out_4));
  Multiplexer #(.width(32), .enable("false")) multiplexer_1 (
    .in0(caculater_1_out_4), .in1({32{1'b0}}), .out(\int ), .sel(or_1_out));

  // Other names for the same wires on the sheet: fraction[9:0] = float[9:0]; exponent[4:0] = float[14:10];
  //   sign = float[15]
endmodule

module caculater (
  input  sign,
  input  [9:0] fraction,
  input  [4:0] exponent,
  output [31:0] out_4
);

  wire choose;
  wire [4:0] subtractor_1_out;
  wire [31:0] bit_extender_1_out, bit_extender_2_out, negator_1_out, result, shifter_1_out;

  Subtractor #(.width(5)) subtractor_1 (
    .a(exponent), .b(5'b01111), .out(subtractor_1_out), .bout(choose));  // open: bin
  Multiplexer #(.width(32), .enable("false")) multiplexer_1 (.in0(result), .in1({32{1'b0}}), .out(out_4), .sel(choose));
  assign bit_extender_1_out = {{21{1'b0}}, {1'b1, fraction}};  // Bit_Extender bit_extender_1
  Shifter #(.width(32)) shifter_1 (.in(bit_extender_1_out), .\dist (subtractor_1_out), .out(shifter_1_out));
  assign bit_extender_2_out = {{10{1'b0}}, shifter_1_out[31:10]};  // Bit_Extender bit_extender_2
  Negator #(.width(32)) negator_1 (.in(bit_extender_2_out), .out(negator_1_out));
  Multiplexer #(.width(32), .enable("false")) multiplexer_2 (
    .in0(bit_extender_2_out), .in1(negator_1_out), .out(result), .sel(sign));
endmodule
