// Logisim project P0_navigation.circ as structural Verilog: 2 circuits, main circuit navigation
module navigation (
  input  [1:0] dir,
  input  clk,
  input  reset,
  output arrive,
  output hit
);

  wire _0_q, _1_q, _2_q, _3_q, _4_q, counter_1_carry, hit_q, s0, s1, s2, s3, status_change_1_hit,
       status_change_1_s0_2, status_change_1_s1_2, status_change_1_s2_2, status_change_1_s3_2,
       status_change_1_s4_2;

  status_change status_change_1 (
    .s4(arrive), .s3(s3), .s2(s2), .s1(s1), .s0(s0), .in_1(dir[1]), .in_0(dir[0]),
    .S4_2(status_change_1_s4_2), .S3_2(status_change_1_s3_2), .S2_2(status_change_1_s2_2),
    .S1_2(status_change_1_s1_2), .S0_2(status_change_1_s0_2), .hit(status_change_1_hit));
  Register #(.width(1)) _4 (.D(status_change_1_s4_2), .Q(_4_q), .clk(clk));  // open: en, clr
  Register #(.width(1)) _3 (.D(status_change_1_s3_2), .Q(_3_q), .clk(clk));  // open: en, clr
  Register #(.width(1)) _2 (.D(status_change_1_s2_2), .Q(_2_q), .clk(clk));  // open: en, clr
  Register #(.width(1)) _1 (.D(status_change_1_s1_2), .Q(_1_q), .clk(clk));  // open: en, clr
  Register #(.width(1)) _0 (.D(status_change_1_s0_2), .Q(_0_q), .clk(clk));  // open: en, clr
  Register #(.width(1)) u_hit (.D(status_change_1_hit), .Q(hit_q), .clk(clk));  // open: en, clr
  Counter #(.width(1), .max('h1), .ongoal("stay")) counter_1 (
    .carry(counter_1_carry), .clk(clk), .clr(reset));  // open: load, D, count, Q
  Multiplexer #(.enable("false")) multiplexer_1 (.in0(1'b0), .in1(_4_q), .out(arrive), .sel(counter_1_carry));
  Multiplexer #(.enable("false")) multiplexer_2 (.in0(1'b0), .in1(_3_q), .out(s3), .sel(counter_1_carry));
  Multiplexer #(.enable("false")) multiplexer_3 (.in0(1'b0), .in1(_2_q), .out(s2), .sel(counter_1_carry));
  Multiplexer #(.enable("false")) multiplexer_4 (.in0(1'b0), .in1(_1_q), .out(s1), .sel(counter_1_carry));
  Multiplexer #(.enable("false")) multiplexer_5 (.in0(1'b1), .in1(_0_q), .out(s0), .sel(counter_1_carry));
  Multiplexer #(.enable("false")) multiplexer_6 (.in0(1'b0), .in1(hit_q), .out(hit), .sel(counter_1_carry));

  // Other names for the same wires on the sheet: in_0 = dir[0]; in_1 = dir[1]; s4 = arrive
endmodule

module status_change (
  input  s4,
  input  s3,
  input  s2,
  input  s1,
  input  s0,
  input  in_1,
  input  in_0,
  output S4_2,
  output S3_2,
  output S2_2,
  output S1_2,
  output S0_2,
  output hit
);

  wire and_1_out, and_2_out, and_3_out, and_4_out, and_5_out, and_6_out, and_7_out, and_8_out, and_9_out,
       and_10_out, and_11_out, and_12_out, and_13_out, and_14_out, and_15_out, and_16_out, not_1_out,
       not_2_out, not_3_out, not_4_out, not_5_out, not_6_out, not_7_out, not_8_out, not_9_out, not_10_out,
       not_11_out, not_12_out, not_13_out, not_14_out, not_15_out, not_16_out, not_17_out, not_18_out,
       not_19_out, not_20_out, not_21_out, not_22_out, not_23_out, not_24_out, not_25_out, not_26_out,
       not_27_out, not_28_out, not_29_out, not_30_out, not_31_out, not_32_out, not_33_out, not_34_out,
       not_35_out, not_36_out;

  not not_1 (not_1_out, s4);
  not not_2 (not_2_out, s2);
  not not_3 (not_3_out, s1);
  not not_4 (not_4_out, s0);
  not not_5 (not_5_out, in_1);
  not not_6 (not_6_out, in_0);
  not not_7 (not_7_out, s4);
  not not_8 (not_8_out, s2);
  not not_9 (not_9_out, s0);
  not not_10 (not_10_out, in_1);
  not not_11 (not_11_out, in_0);
  not not_12 (not_12_out, s4);
  not not_13 (not_13_out, s3);
  not not_14 (not_14_out, s0);
  not not_15 (not_15_out, in_1);
  not not_16 (not_16_out, in_0);
  not not_17 (not_17_out, s4);
  not not_18 (not_18_out, s2);
  not not_19 (not_19_out, s0);
  not not_20 (not_20_out, in_1);
  not not_21 (not_21_out, in_0);
  not not_22 (not_22_out, in_0);
  not not_23 (not_23_out, in_0);
  not not_24 (not_24_out, s4);
  not not_25 (not_25_out, s2);
  not not_26 (not_26_out, s1);
  not not_27 (not_27_out, in_1);
  not not_28 (not_28_out, s4);
  not not_29 (not_29_out, s2);
  not not_30 (not_30_out, s1);
  not not_31 (not_31_out, in_0);
  not not_32 (not_32_out, s4);
  not not_33 (not_33_out, s3);
  not not_34 (not_34_out, in_1);
  not not_35 (not_35_out, in_0);
  and and_1 (and_1_out, not_1_out, not_2_out, not_3_out, not_4_out, not_5_out, not_6_out);
  not not_36 (not_36_out, in_1);
  and and_2 (and_2_out, s2, not_36_out, in_0);
  and and_3 (and_3_out, not_7_out, not_8_out, not_9_out, not_10_out, in_0);
  and and_4 (and_4_out, s3, in_1, not_11_out);
  and and_5 (and_5_out, not_12_out, not_13_out, not_14_out, not_15_out, not_16_out);
  and and_6 (and_6_out, s2, in_1, in_0);
  and and_7 (and_7_out, not_17_out, not_18_out, not_19_out, in_1, in_0);
  and and_8 (and_8_out, s0, not_20_out, not_21_out);
  and and_9 (and_9_out, s2, in_1, not_22_out);
  and and_10 (and_10_out, s0, in_0);
  and and_11 (and_11_out, s0, in_1);
  and and_12 (and_12_out, s1, in_1, not_23_out);
  and and_13 (and_13_out, not_24_out, not_25_out, not_26_out, not_27_out, in_0);
  and and_14 (and_14_out, not_28_out, not_29_out, not_30_out, in_1, not_31_out);
  and and_15 (and_15_out, not_32_out, not_33_out, in_1, in_0);
  and and_16 (and_16_out, s2, not_34_out, not_35_out);
  or or_1 (S4_2, and_1_out, and_2_out);
  or or_2 (S3_2, and_3_out, and_4_out);
  or or_3 (S2_2, and_5_out, and_6_out);
  or or_4 (S1_2, and_7_out, and_8_out, and_9_out);
  or or_5 (S0_2, and_10_out, and_11_out, and_12_out, s4);
  or or_6 (hit, and_13_out, and_14_out, and_15_out, and_16_out);
endmodule
