// Logisim project single_cpu.circ as structural Verilog: 11 circuits, main circuit main
module main (
  input  in_1,
  output [31:0] out_2,
  output out_3,
  output [4:0] out_4,
  output [31:0] out_5,
  output out_6,
  output [4:0] out_7,
  output [31:0] out_8
);

  wire ALUSrc, clk, EXTop;
  wire [1:0] Memback, RegDst, shiftop;
  wire [2:0] ALUControl, Cmp, Move;
  wire [31:0] adder_1_out, alu_1_y, dm_1_out_6, ext_imm, grf_rs, multiplexer_2_out, npc_1_npc, PC;

  Clock clock_1 (.out(clk));
  NPC npc_1 (
    .PC(PC), .offset(ext_imm), .Move(Move), .instr_index(out_2[25:0]), .NPC(npc_1_npc), .GRF_rs(grf_rs),
    .Cmp(Cmp));
  IFU ifu_1 (.in_1(clk), .in_2(in_1), .out_4(out_2), .PC(PC), .in_3(npc_1_npc));
  EXT ext_1 (.in_1(out_2[15:0]), .in_2(EXTop), .out_4(ext_imm), .shiftop(shiftop));
  Control_Unit control_unit_1 (
    .op(out_2[31:26]), .funct(out_2[5:0]), .out_3(shiftop), .out_4(EXTop), .out_5(Memback), .out_6(out_6),
    .out_7(ALUSrc), .out_8(out_3), .out_11(RegDst), .out_9(ALUControl), .move(Move));
  Multiplexer #(.select(2), .width(5), .enable("false")) multiplexer_1 (
    .in0(out_2[20:16]), .in1(out_2[15:11]), .in2({5{1'b1}}), .out(out_4), .sel(RegDst));  // open: in3
  GRF grf_1 (
    .in_1(clk), .in_2(in_1), .in_3(out_3), .A1(out_2[25:21]), .A2(out_2[20:16]), .A3(out_4), .RD1(grf_rs),
    .WD(out_5), .RD2(out_8));
  Multiplexer #(.width(32), .enable("false")) multiplexer_2 (
    .in0(out_8), .in1(ext_imm), .out(multiplexer_2_out), .sel(ALUSrc));
  ALU alu_1 (
    .A(grf_rs), .B(multiplexer_2_out), .Control(ALUControl), .Y({alu_1_y[31:7], out_7, alu_1_y[1:0]}),
    .compare(Cmp));
  DM dm_1 (
    .in_1(clk), .in_2(out_6), .in_3(in_1), .in_4({alu_1_y[31:7], out_7, alu_1_y[1:0]}), .in_5(out_8),
    .out_6(dm_1_out_6));
  Adder #(.width(32)) adder_1 (.a(PC), .b(32'h4), .out(adder_1_out));  // open: cin, cout
  Multiplexer #(.select(2), .width(32), .enable("false")) multiplexer_3 (
    .in0({alu_1_y[31:7], out_7, alu_1_y[1:0]}), .in1(dm_1_out_6), .in2(adder_1_out), .out(out_5),
    .sel(Memback));  // open: in3

  // Other names for the same wires on the sheet: MemAddr[4:0] = out_7; Instr[31:0] = out_2; op[5:0] = out_2[31:26];
  //   funct[5:0] = out_2[5:0]; imm[15:0] = out_2[15:0]; instr_index[25:0] = out_2[25:0]; rd[4:0] = out_2[15:11];
  //   rt[4:0] = out_2[20:16]; rs[4:0] = out_2[25:21]; MemData[31:0] = out_8; MemWrite = out_6; RegAddr[4:0] = out_4;
  //   RegData[31:0] = out_5; RegWrite = out_3; reset = in_1
endmodule

module GRF (
  input  in_1,
  input  in_2,
  input  in_3,
  input  [4:0] A1,
  input  [4:0] A2,
  input  [4:0] A3,
  input  [31:0] WD,
  output [31:0] RD1,
  output [31:0] RD2
);

  wire _0, _1, _2, _3, _4, _5, _6, _7, _8, _9, _10, _11, _12, _13, _14, _15, _16, _17, _18, _19, _20, _21,
       _22, _23, _24, _25, _26, _27, _28, _29, _30, _31;
  wire [31:0] out_0, out_1, out_2, out_3, out_4, out_5, out_6, out_7, out_8, out_9, out_10, out_11, out_12,
       out_13, out_14, out_15, out_16, out_17, out_18, out_19, out_20, out_21, out_22, out_23, out_24,
       out_25, out_26, out_27, out_28, out_29, out_30, out_31;

  Demultiplexer #(.select(5), .disabled(0), .enable("false")) demultiplexer_1 (
    .out0(_0), .out1(_1), .out2(_2), .out3(_3), .out4(_4), .out5(_5), .out6(_6), .out7(_7), .out8(_8),
    .out9(_9), .out10(_10), .out11(_11), .out12(_12), .out13(_13), .out14(_14), .out15(_15), .out16(_16),
    .out17(_17), .out18(_18), .out19(_19), .out20(_20), .out21(_21), .out22(_22), .out23(_23), .out24(_24),
    .out25(_25), .out26(_26), .out27(_27), .out28(_28), .out29(_29), .out30(_30), .out31(_31), .in(in_3),
    .sel(A3));
  Register #(.width(32)) zero (.D(WD), .en(_0), .Q(out_0), .clk(in_1), .clr(1'b1));
  Register #(.width(32)) at (.D(WD), .en(_1), .Q(out_1), .clk(in_1), .clr(in_2));
  Register #(.width(32)) v0 (.D(WD), .en(_2), .Q(out_2), .clk(in_1), .clr(in_2));
  Register #(.width(32)) v1 (.D(WD), .en(_3), .Q(out_3), .clk(in_1), .clr(in_2));
  Register #(.width(32)) a0 (.D(WD), .en(_4), .Q(out_4), .clk(in_1), .clr(in_2));
  Register #(.width(32)) u_a1 (.D(WD), .en(_5), .Q(out_5), .clk(in_1), .clr(in_2));
  Register #(.width(32)) u_a2 (.D(WD), .en(_6), .Q(out_6), .clk(in_1), .clr(in_2));
  Register #(.width(32)) u_a3 (.D(WD), .en(_7), .Q(out_7), .clk(in_1), .clr(in_2));
  Register #(.width(32)) t0 (.D(WD), .en(_8), .Q(out_8), .clk(in_1), .clr(in_2));
  Register #(.width(32)) t1 (.D(WD), .en(_9), .Q(out_9), .clk(in_1), .clr(in_2));
  Register #(.width(32)) t2 (.D(WD), .en(_10), .Q(out_10), .clk(in_1), .clr(in_2));
  Register #(.width(32)) t3 (.D(WD), .en(_11), .Q(out_11), .clk(in_1), .clr(in_2));
  Register #(.width(32)) t4 (.D(WD), .en(_12), .Q(out_12), .clk(in_1), .clr(in_2));
  Register #(.width(32)) t5 (.D(WD), .en(_13), .Q(out_13), .clk(in_1), .clr(in_2));
  Register #(.width(32)) t6 (.D(WD), .en(_14), .Q(out_14), .clk(in_1), .clr(in_2));
  Register #(.width(32)) t7 (.D(WD), .en(_15), .Q(out_15), .clk(in_1), .clr(in_2));
  Register #(.width(32)) s0 (.D(WD), .en(_16), .Q(out_16), .clk(in_1), .clr(in_2));
  Register #(.width(32)) s1 (.D(WD), .en(_17), .Q(out_17), .clk(in_1), .clr(in_2));
  Register #(.width(32)) s2 (.D(WD), .en(_18), .Q(out_18), .clk(in_1), .clr(in_2));
  Register #(.width(32)) s3 (.D(WD), .en(_19), .Q(out_19), .clk(in_1), .clr(in_2));
  Register #(.width(32)) s4 (.D(WD), .en(_20), .Q(out_20), .clk(in_1), .clr(in_2));
  Register #(.width(32)) s5 (.D(WD), .en(_21), .Q(out_21), .clk(in_1), .clr(in_2));
  Register #(.width(32)) s6 (.D(WD), .en(_22), .Q(out_22), .clk(in_1), .clr(in_2));
  Register #(.width(32)) s7 (.D(WD), .en(_23), .Q(out_23), .clk(in_1), .clr(in_2));
  Register #(.width(32)) t8 (.D(WD), .en(_24), .Q(out_24), .clk(in_1), .clr(in_2));
  Register #(.width(32)) t9 (.D(WD), .en(_25), .Q(out_25), .clk(in_1), .clr(in_2));
  Register #(.width(32)) k0 (.D(WD), .en(_26), .Q(out_26), .clk(in_1), .clr(in_2));
  Register #(.width(32)) k1 (.D(WD), .en(_27), .Q(out_27), .clk(in_1), .clr(in_2));
  Register #(.width(32)) gp (.D(WD), .en(_28), .Q(out_28), .clk(in_1), .clr(in_2));
  Register #(.width(32)) sp (.D(WD), .en(_29), .Q(out_29), .clk(in_1), .clr(in_2));
  Register #(.width(32)) fp (.D(WD), .en(_30), .Q(out_30), .clk(in_1), .clr(in_2));
  Register #(.width(32)) ra (.D(WD), .en(_31), .Q(out_31), .clk(in_1), .clr(in_2));
  Multiplexer #(.select(5), .width(32), .disabled(0), .enable("false")) multiplexer_1 (
    .in0(out_0), .in1(out_1), .in2(out_2), .in3(out_3), .in4(out_4), .in5(out_5), .in6(out_6), .in7(out_7),
    .in8(out_8), .in9(out_9), .in10(out_10), .in11(out_11), .in12(out_12), .in13(out_13), .in14(out_14),
    .in15(out_15), .in16(out_16), .in17(out_17), .in18(out_18), .in19(out_19), .in20(out_20), .in21(out_21),
    .in22(out_22), .in23(out_23), .in24(out_24), .in25(out_25), .in26(out_26), .in27(out_27), .in28(out_28),
    .in29(out_29), .in30(out_30), .in31(out_31), .out(RD1), .sel(A1));
  Multiplexer #(.select(5), .width(32), .disabled(0), .enable("false")) multiplexer_2 (
    .in0(out_0), .in1(out_1), .in2(out_2), .in3(out_3), .in4(out_4), .in5(out_5), .in6(out_6), .in7(out_7),
    .in8(out_8), .in9(out_9), .in10(out_10), .in11(out_11), .in12(out_12), .in13(out_13), .in14(out_14),
    .in15(out_15), .in16(out_16), .in17(out_17), .in18(out_18), .in19(out_19), .in20(out_20), .in21(out_21),
    .in22(out_22), .in23(out_23), .in24(out_24), .in25(out_25), .in26(out_26), .in27(out_27), .in28(out_28),
    .in29(out_29), .in30(out_30), .in31(out_31), .out(RD2), .sel(A2));

  // Other names for the same wires on the sheet: clk = in_1; input[31:0] = WD; reset = in_2; WE = in_3
endmodule

module ALU (
  input  [31:0] A,
  input  [31:0] B,
  input  [2:0] Control,
  output [31:0] Y,
  output [2:0] compare
);

  wire [31:0] adder_1_out, and_1_out, bit_extender_1_out, or_1_out, subtractor_1_out;

  Comparator #(.width(32), .mode("unsigned")) comparator_1 (
    .a(A), .b(B), .gt(compare[0]), .eq(compare[1]), .lt(compare[2]));
  assign and_1_out = A & B;  // AND_Gate and_1, 32 bits wide
  assign or_1_out = A | B;  // OR_Gate or_1, 32 bits wide
  Adder #(.width(32)) adder_1 (.a(A), .b(B), .out(adder_1_out));  // open: cin, cout
  Subtractor #(.width(32)) subtractor_1 (.a(A), .b(B), .out(subtractor_1_out));  // open: bin, bout
  assign bit_extender_1_out = {{31{1'b0}}, compare[2]};  // Bit_Extender bit_extender_1
  Multiplexer #(.select(3), .width(32), .enable("false")) multiplexer_1 (
    .in0(and_1_out), .in1(or_1_out), .in2(adder_1_out), .in6(subtractor_1_out), .in7(bit_extender_1_out),
    .out(Y), .sel(Control));  // open: in3, in4, in5
endmodule

module EXT (
  input  [15:0] in_1,
  input  in_2,
  input  [1:0] shiftop,
  output [31:0] out_4
);

  wire [4:0] multiplexer_2_out;
  wire [31:0] bit_extender_1_out, bit_extender_2_out, multiplexer_1_out;

  assign bit_extender_1_out = {{16{1'b0}}, in_1};  // Bit_Extender bit_extender_1
  assign bit_extender_2_out = {{16{in_1[15]}}, in_1};  // Bit_Extender bit_extender_2
  Multiplexer #(.width(32), .enable("false")) multiplexer_1 (
    .in0(bit_extender_1_out), .in1(bit_extender_2_out), .out(multiplexer_1_out), .sel(in_2));
  Multiplexer #(.select(2), .width(5), .enable("false")) multiplexer_2 (
    .in0({5{1'b0}}), .in1(5'b00010), .in2(5'b10000), .out(multiplexer_2_out), .sel(shiftop));  // open: in3
  Shifter #(.width(32)) shifter_1 (.in(multiplexer_1_out), .\dist (multiplexer_2_out), .out(out_4));
endmodule

module DM (
  input  in_1,
  input  in_2,
  input  in_3,
  input  [31:0] in_4,
  input  [31:0] in_5,
  output [31:0] out_6
);

  RAM #(.addrWidth(10), .dataWidth(32), .bus("separate")) ram_1 (
    .addr(in_4[11:2]), .din(in_5), .data(out_6), .str(in_2), .clk(in_1), .clr(in_3));  // open: sel, ld

  // Other names for the same wires on the sheet: A[31:0] = in_4; clk = in_1; reset = in_3; WD[31:0] = in_5; WE = in_2
endmodule

module IFU (
  input  in_1,
  input  in_2,
  input  [31:0] in_3,
  output [31:0] out_4,
  output [31:0] PC
);

  Register #(.width(32)) register_1 (.D(in_3), .Q(PC), .clk(in_1), .clr(in_2));  // open: en
  IM im_1 (.RD(out_4), .in_1(PC));

  // Other names for the same wires on the sheet: clk = in_1; reset = in_2
endmodule

module NPC (
  input  [2:0] Move,
  input  [2:0] Cmp,
  input  [31:0] PC,
  input  [31:0] offset,
  input  [25:0] instr_index,
  input  [31:0] GRF_rs,
  output [31:0] NPC
);

  wire Beq;
  wire [31:0] adder_1_out, adder_2_out, multiplexer_1_out, multiplexer_2_out;

  and and_1 (Beq, Cmp[1], Move[0]);
  Multiplexer #(.width(32), .enable("false")) multiplexer_1 (
    .in0({32{1'b0}}), .in1(offset), .out(multiplexer_1_out), .sel(Beq));
  Adder #(.width(32)) adder_1 (.a(32'h4), .b(PC), .out(adder_1_out));  // open: cin, cout
  Adder #(.width(32)) adder_2 (.a(adder_1_out), .b(multiplexer_1_out), .out(adder_2_out));  // open: cin, cout
  Multiplexer #(.width(32), .enable("false")) multiplexer_2 (
    .in0(adder_2_out), .in1({PC[31:28], instr_index, 2'b00}), .out(multiplexer_2_out), .sel(Move[1]));
  Multiplexer #(.width(32), .enable("false")) multiplexer_3 (
    .in0(multiplexer_2_out), .in1(GRF_rs), .out(NPC), .sel(Move[2]));

  // Other names for the same wires on the sheet: PC31_28[3:0] = PC[31:28]
endmodule

module IM (
  input  [31:0] in_1,
  output [31:0] RD
);

  ROM #(.addrWidth(10), .dataWidth(32)) rom_1 (.addr(in_1[11:2]), .data(RD));  // open: sel

  // Other names for the same wires on the sheet: A[31:0] = in_1

  // Notes on the sheet:
  //   contents of rom_1 (hex, n*v repeats v):
  //   c000c01
endmodule

module Control_Unit (
  input  [5:0] op,
  input  [5:0] funct,
  output [1:0] out_3,
  output out_4,
  output [1:0] out_5,
  output out_6,
  output out_7,
  output out_8,
  output [2:0] out_9,
  output [2:0] move,
  output [1:0] out_11
);

  wire main_decoder_1_out_12, main_decoder_1_out_13;

  Main_Decoder main_decoder_1 (
    .op5(op[5]), .op4(op[4]), .op3(op[3]), .op2(op[2]), .op1(op[1]), .op0(op[0]), .out_7(out_8),
    .out_15(out_11), .out_8(out_7), .out_9(move[0]), .out_10(out_6), .out_17(out_5), .out_11(out_4),
    .out_12(main_decoder_1_out_12), .out_13(main_decoder_1_out_13), .out_16(out_3), .out_14(move[1]));
  ALU_Decoder alu_decoder_1 (
    .funct5(funct[5]), .funct4(funct[4]), .funct3(funct[3]), .funct2(funct[2]), .funct1(funct[1]),
    .funct0(funct[0]), .in_1(main_decoder_1_out_12), .in_2(main_decoder_1_out_13), .out_10(out_9),
    .out_9(move[2]));

  // Other names for the same wires on the sheet: ALUSrc = out_7; EXTop = out_4; Memback[1:0] = out_5;
  //   MemWrite = out_6; Branch = move[0]; Jump = move[1]; jr = move[2]; RegDst[1:0] = out_11; RegWrite = out_8;
  //   shiftop[1:0] = out_3
endmodule

module Main_Decoder (
  input  op5,
  input  op4,
  input  op3,
  input  op2,
  input  op1,
  input  op0,
  output out_7,
  output out_8,
  output out_9,
  output out_10,
  output out_11,
  output out_12,
  output out_13,
  output out_14,
  output [1:0] out_15,
  output [1:0] out_16,
  output [1:0] out_17
);

  wire addi, beq, j, jal, lui, lw, not_1_out, not_2_out, not_3_out, not_4_out, not_5_out, not_6_out, ori,
       Rtype, sw;

  not not_1 (not_1_out, op5);
  not not_2 (not_2_out, op4);
  not not_3 (not_3_out, op3);
  not not_4 (not_4_out, op2);
  not not_5 (not_5_out, op1);
  not not_6 (not_6_out, op0);
  and u_lw (lw, op0, op1, not_4_out, not_3_out, not_2_out, op5);
  and u_sw (sw, op0, op1, not_4_out, op3, not_2_out, op5);
  and u_beq (beq, not_6_out, not_5_out, op2, not_3_out, not_2_out, not_1_out);
  and u_Rtype (Rtype, not_6_out, not_5_out, not_4_out, not_3_out, not_2_out, not_1_out);
  and u_ori (ori, op0, not_5_out, op2, op3, not_2_out, not_1_out);
  and u_lui (lui, op0, op1, op2, op3, not_2_out, not_1_out);
  and u_addi (addi, not_6_out, not_5_out, not_4_out, op3, not_2_out, not_1_out);
  and u_j (j, not_6_out, op1, not_4_out, not_3_out, not_2_out, not_1_out);
  and u_jal (jal, op0, op1, not_4_out, not_3_out, not_2_out, not_1_out);
  or RegWirte (out_7, jal, lui, ori, Rtype, lw, addi);
  buf RegDst1 (out_15[1], jal);  // OR_Gate
  buf RegDst0 (out_15[0], Rtype);  // OR_Gate
  or ALUSrc (out_8, lui, ori, sw, lw, addi);
  buf Branch (out_9, beq);  // OR_Gate
  buf MemWrite (out_10, sw);  // OR_Gate
  buf Memback1 (out_17[1], jal);  // OR_Gate
  buf Memback0 (out_17[0], lw);  // OR_Gate
  or EXTop (out_11, sw, beq, lw, addi);
  or ALUop1 (out_12, ori, Rtype);
  or ALUop0 (out_13, beq, Rtype);
  buf shiftop1 (out_16[1], lui);  // OR_Gate
  buf shiftop0 (out_16[0], beq);  // OR_Gate
  or Jump (out_14, j, jal);
endmodule

module ALU_Decoder (
  input  in_1,
  input  in_2,
  input  funct5,
  input  funct4,
  input  funct3,
  input  funct2,
  input  funct1,
  input  funct0,
  output out_9,
  output [2:0] out_10
);

  wire addu, addu_out, \and , and_1_out, and_2_out, and_3_out, and_5_out, and_6_out, and_9_out, and_10_out,
       and_11_out, jr_out, not_1_out, not_2_out, not_3_out, not_4_out, not_5_out, not_6_out, \or , or_out,
       slt, slt_out, subu, subu_out;

  not not_1 (not_1_out, funct4);
  not not_2 (not_2_out, funct5);
  not not_3 (not_3_out, funct2);
  not not_4 (not_4_out, funct3);
  not not_5 (not_5_out, funct1);
  not not_6 (not_6_out, funct0);
  and and_1 (and_1_out, in_2, in_1);
  and and_2 (and_2_out, and_1_out, addu_out);
  and u_addu (addu_out, funct0, not_5_out, not_3_out, not_4_out, not_1_out, funct5);
  and and_3 (and_3_out, and_1_out, subu_out);
  and u_subu (subu_out, funct0, funct1, not_3_out, not_4_out, not_1_out, funct5);
  and and_4 (\and , and_1_out, and_5_out);
  and and_5 (and_5_out, not_6_out, not_5_out, funct2, not_4_out, not_1_out, funct5);
  and and_6 (and_6_out, and_1_out, or_out);
  and u_or (or_out, funct0, not_5_out, funct2, not_4_out, not_1_out, funct5);
  and and_7 (slt, and_1_out, slt_out);
  and u_slt (slt_out, not_6_out, funct1, not_3_out, funct3, not_1_out, funct5);
  and and_8 (out_9, and_1_out, jr_out);
  and jr (jr_out, not_6_out, not_5_out, not_3_out, funct3, not_1_out, not_2_out);
  and and_9 (and_9_out, ~in_2, ~in_1);  // AND_Gate
  and and_10 (and_10_out, in_2, ~in_1);  // AND_Gate
  and and_11 (and_11_out, ~in_2, in_1);  // AND_Gate
  or or_2 (\or , and_11_out, and_6_out);
  or or_3 (addu, and_9_out, and_2_out);
  or or_4 (subu, and_10_out, and_3_out);
  or ALUcon2 (out_10[2], subu, slt);
  or ALUcon1 (out_10[1], addu, subu, slt);
  or ALUcon0 (out_10[0], \or , slt);

  // Other names for the same wires on the sheet: ALUop0 = in_2; ALUop1 = in_1
endmodule
